# Fritzing sketch esquematico-termometro (saved by Fritzing 0.9.0b)

parts:
  LED1 = LED - 5mm [color="Red (633nm)" package="5 mm [THT]"]
  LCD1 = LCD screen
  Part1 = Arduino Uno (Rev3)
  T1 = LM35 Temperature Sensor [package="TO92 [THT]"]
  SD_card_module1 = SD Card Module
  Part3 = Real Time Clock Breakout - DS1307 [part_number=147824]

nets:
  GND: LED1.cathode, LCD1.VSS, LCD1.R/W, LCD1.LED-, Part1.GND, T1.GND, SD_card_module1.GND, Part3.GND
  N1: LED1.anode, Part1.D2
  VDD: LCD1.VDD, LCD1.LED+, Part1.5V, T1.+Vs, Part3.VCC
  N2: LCD1.V0, Part1.D9_PWM
  N3: LCD1.RS, Part1.D8
  N4: LCD1.E, Part1.D7
  N5: LCD1.DB4, Part1.D6_PWM
  N6: LCD1.DB5, Part1.D5_PWM
  N7: LCD1.DB6, Part1.D4
  N8: LCD1.DB7, Part1.D3_PWM
  N9: Part1.A0, T1.Vout
  N10: Part1.A1, Part3.SCL
  N11: Part1.A2, Part3.SDA
  N12: Part1.D10_PWM/SS, SD_card_module1.CS
  N13: Part1.D11_PWM/MOSI, SD_card_module1.MOSI
  N14: Part1.D12/MISO, SD_card_module1.MISO
  N15: Part1.D13/SCK, SD_card_module1.SCK
  N16: Part1.3V3, SD_card_module1.+3.3

custom parts:
  SD Card Module: SD Card Module Slot Socket Reader For Arduino ARM MCU
  Real Time Clock Breakout - DS1307: Two wire I2C interface; Hour : Minutes : Seconds AM/PM Day Month, Date - Year; Leap year compensation; Accurate calendar up to year 2100; DS1307 based RTC with LIR2032 battery (Battery include); 56 Bytes of Non-volatile memory available to user; Working time: 1 year
